// Logisim project HA.circ as structural Verilog: 2 circuits, main circuit main
module main (
  input  A,
  input  B,
  input  Cin,
  output Finalcarry,
  output Finalout
);

  wire ha_1_c, ha_1_d, ha_2_c;

  HA ha_1 (.A(A), .B(B), .C(ha_1_c), .D(ha_1_d));
  HA ha_2 (.A(ha_1_d), .B(Cin), .C(ha_2_c), .D(Finalout));
  or or_1 (Finalcarry, ha_1_c, ha_2_c);
endmodule

module HA (
  input  A,
  input  B,
  output C,
  output D
);

  and and_1 (C, A, B);
  xor xor_1 (D, A, B);
endmodule
