// Logisim project Lab_6_Template.circ as structural Verilog: 11 circuits, main circuit main
module main (
  input  en
);

  wire b0, b1, b2, b3, b4, b5, b6, c0, c1, c2, c3, c4, c5, c6, clk_out;
  wire [3:0] downcounter_testing_1_count;
  wire [7:7] Bin2Hex_1_hex0, Bin2Hex_1_hex1;

  Clock clk (.out(clk_out));
  DownCounter_Testing downcounter_testing_1 (.en(en), .clk(clk_out), .count(downcounter_testing_1_count));
  _7_Segment_Display #(.active("false")) L_7_Segment_Display_3 (
    .g(b6), .f(b5), .a(b0), .b(b1), .e(b4), .d(b3), .c(b2), .dp(1'b1));
  _7_Segment_Display #(.active("false")) L_7_Segment_Display_4 (
    .g(c6), .f(c5), .a(c0), .b(c1), .e(c4), .d(c3), .c(c2), .dp(1'b1));
  Bin2Hex Bin2Hex_1 (
    .v3(downcounter_testing_1_count[3]), .v2(downcounter_testing_1_count[2]),
    .v1(downcounter_testing_1_count[1]), .v0(downcounter_testing_1_count[0]),
    .HEX1({Bin2Hex_1_hex1[7], b6, b5, b4, b3, b2, b1, b0}),
    .HEX0({Bin2Hex_1_hex0[7], c6, c5, c4, c3, c2, c1, c0}));

  // Notes on the sheet:
  //   Counter Display
endmodule

module Seg7_Decoder (
  input  i_m3,
  input  i_m2,
  input  i_m1,
  input  i_m0,
  output [7:0] o_seg
);

  wire and_1_out, and_2_out, and_3_out, and_4_out, and_5_out, and_6_out, and_7_out, and_8_out, and_9_out,
       and_10_out, and_11_out, and_12_out, and_13_out, and_14_out, and_15_out, and_16_out, and_17_out,
       and_18_out, and_19_out, and_20_out, and_21_out, and_22_out, and_23_out, not_1_out, not_2_out,
       not_3_out, not_4_out;

  not not_1 (not_1_out, i_m3);
  not not_2 (not_2_out, i_m2);
  not not_3 (not_3_out, i_m1);
  not not_4 (not_4_out, i_m0);
  and and_1 (and_1_out, not_1_out, not_2_out, not_3_out);
  and and_2 (and_2_out, not_1_out, i_m2, i_m1, i_m0);
  and and_3 (and_3_out, i_m3, not_2_out, i_m1);
  and and_4 (and_4_out, not_1_out, not_2_out, i_m0);
  and and_5 (and_5_out, not_1_out, not_2_out, i_m1);
  and and_6 (and_6_out, not_2_out, i_m1, i_m0);
  and and_7 (and_7_out, i_m3, i_m2, not_3_out);
  and and_8 (and_8_out, not_1_out, i_m2, not_3_out);
  and and_9 (and_9_out, i_m3, i_m2, i_m1);
  and and_10 (and_10_out, not_1_out, not_2_out, not_3_out, i_m0);
  and and_11 (and_11_out, not_1_out, i_m2, not_3_out, not_4_out);
  and and_12 (and_12_out, not_1_out, i_m2, i_m1, i_m0);
  and and_13 (and_13_out, i_m3, not_2_out, i_m1, i_m0);
  and and_14 (and_14_out, i_m3, i_m2, i_m1, not_4_out);
  and and_15 (and_15_out, not_1_out, not_2_out, i_m1, not_4_out);
  and and_16 (and_16_out, i_m3, i_m2, not_3_out, not_4_out);
  and and_17 (and_17_out, not_1_out, i_m2, not_3_out, i_m0);
  and and_18 (and_18_out, not_1_out, i_m2, i_m1, not_4_out);
  and and_19 (and_19_out, i_m3, i_m2, i_m1, i_m0);
  and and_20 (and_20_out, not_1_out, not_2_out, not_3_out, i_m0);
  and and_21 (and_21_out, not_1_out, i_m2, not_3_out, not_4_out);
  and and_22 (and_22_out, i_m3, not_2_out, i_m1, i_m0);
  and and_23 (and_23_out, i_m3, i_m2, i_m1, not_4_out);
  or or_1 (o_seg[6], and_1_out, and_2_out, and_3_out);
  or or_2 (o_seg[5], and_4_out, and_5_out, and_6_out, and_7_out);
  or or_3 (o_seg[4], i_m0, and_8_out, and_9_out);
  or or_4 (o_seg[3], and_10_out, and_11_out, and_12_out, and_13_out, and_14_out);
  or or_5 (o_seg[2], and_15_out, and_16_out);
  or or_6 (o_seg[1], and_17_out, and_18_out, and_19_out);
  or or_7 (o_seg[0], and_20_out, and_21_out, and_22_out, and_23_out);

  assign o_seg[7] = 1'b1;
endmodule

module CircuitA (
  input  i2,
  input  i1,
  input  i0,
  output o2,
  output o1,
  output o0
);

  not not_1 (o1, i1);
  and and_1 (o2, i2, i1);

  assign o0 = i0;
endmodule

module myComparator (
  input  v3,
  input  v2,
  input  v1,
  input  v0,
  output z
);

  wire and_1_out, and_2_out;

  and and_1 (and_1_out, v3, v1);
  and and_2 (and_2_out, v3, v2);
  or or_1 (z, and_1_out, and_2_out);
endmodule

module CircuitB (
  input  z,
  output s6,
  output s5,
  output s4,
  output s3,
  output s2,
  output s1,
  output s0
);


  assign s0 = z;
  assign s1 = 1'b0;
  assign s2 = 1'b0;
  assign s3 = z;
  assign s4 = z;
  assign s5 = z;
  assign s6 = 1'b1;
endmodule

module Bin2Hex (
  input  v3,
  input  v2,
  input  v1,
  input  v0,
  output [7:0] HEX1,
  output [7:0] HEX0
);

  wire z;

  myComparator myComparator_1 (.v3(v3), .v2(v2), .v1(v1), .v0(v0), .z(z));
  CircuitB CircuitB_1 (
    .z(z), .s6(HEX1[6]), .s5(HEX1[5]), .s4(HEX1[4]), .s3(HEX1[3]), .s2(HEX1[2]), .s1(HEX1[1]), .s0(HEX1[0]));
  Seg7_Decoder Seg7_Decoder_1 (.i_m3(v3), .i_m2(v2), .i_m1(v1), .i_m0(v0), .o_seg(HEX0));

  assign HEX1[7] = 1'b1;
endmodule

module UpCounter_Template (
  input  en,
  input  clk,
  output [3:0] count
);

  wire t_ff_1_qn, t_ff_2_qn, t_ff_3_qn;

  T_Flip_Flop t_ff_1 (.T(en), .clk(clk), .Q(count[0]), .Qn(t_ff_1_qn));  // open: reset, preset
  T_Flip_Flop t_ff_2 (.T(en), .clk(t_ff_1_qn), .Q(count[1]), .Qn(t_ff_2_qn));  // open: reset, preset
  T_Flip_Flop t_ff_3 (.T(en), .clk(t_ff_2_qn), .Q(count[2]), .Qn(t_ff_3_qn));  // open: reset, preset
  T_Flip_Flop t_ff_4 (.T(en), .clk(t_ff_3_qn), .Q(count[3]));  // open: Qn, reset, preset
endmodule

module DownCounter_Template (
  input  en,
  input  clk,
  output [3:0] count
);

  T_Flip_Flop t_ff_1 (.T(en), .clk(clk), .Q(count[0]));  // open: Qn, reset, preset
  T_Flip_Flop t_ff_2 (.T(en), .clk(count[0]), .Q(count[1]));  // open: Qn, reset, preset
  T_Flip_Flop t_ff_3 (.T(en), .clk(count[1]), .Q(count[2]));  // open: Qn, reset, preset
  T_Flip_Flop t_ff_4 (.T(en), .clk(count[2]), .Q(count[3]));  // open: Qn, reset, preset
endmodule

module Mod5_Template (
  input  en,
  input  clk,
  output [2:0] count
);

  wire and_1_out, nand_1_out, not_1_out, not_2_out, not_3_out;

  T_Flip_Flop t_ff_1 (.T(en), .clk(clk), .Q(count[2]), .reset(not_1_out));  // open: Qn, preset
  not not_1 (not_1_out, nand_1_out);
  T_Flip_Flop t_ff_2 (.T(count[2]), .clk(clk), .Q(count[1]), .reset(not_2_out));  // open: Qn, preset
  not not_2 (not_2_out, nand_1_out);
  and and_1 (and_1_out, count[2], count[1]);
  T_Flip_Flop t_ff_3 (.T(and_1_out), .clk(clk), .Q(count[0]), .reset(not_3_out));  // open: Qn, preset
  not not_3 (not_3_out, nand_1_out);
  nand nand_1 (nand_1_out, count[2], count[0]);
endmodule

module Johnson_Counter_Template (
  input  reset,
  input  clk,
  output [3:0] count
);

  wire d_ff_4_qn;

  D_Flip_Flop d_ff_1 (.D(d_ff_4_qn), .clk(clk), .Q(count[0]), .reset(reset));  // open: Qn, preset
  D_Flip_Flop d_ff_2 (.D(count[0]), .clk(clk), .Q(count[1]), .reset(reset));  // open: Qn, preset
  D_Flip_Flop d_ff_3 (.D(count[1]), .clk(clk), .Q(count[2]), .reset(reset));  // open: Qn, preset
  D_Flip_Flop d_ff_4 (.D(count[2]), .clk(clk), .Q(count[3]), .Qn(d_ff_4_qn), .reset(reset));  // open: preset
endmodule

module DownCounter_Testing (
  input  en,
  input  clk,
  output [3:0] count
);

  wire nor_1_out;

  T_Flip_Flop t_ff_1 (.T(en), .clk(clk), .Q(count[0]), .reset(nor_1_out));  // open: Qn, preset
  T_Flip_Flop t_ff_2 (.T(en), .clk(count[0]), .Q(count[1]), .preset(nor_1_out));  // open: Qn, reset
  T_Flip_Flop t_ff_3 (.T(en), .clk(count[1]), .Q(count[2]), .reset(nor_1_out));  // open: Qn, preset
  nor nor_1 (nor_1_out, count[0], count[1], clk, count[2], count[3]);
  T_Flip_Flop t_ff_4 (.T(en), .clk(count[2]), .Q(count[3]), .preset(nor_1_out));  // open: Qn, reset
endmodule
