// Logisim project Lab_08.circ as structural Verilog: 3 circuits, main circuit main
module main (
  input  Input_1,
  input  input_2,
  input  input_3,
  output LED1,
  output LED2,
  output LED3
);

  wire and_1_out, and_2_out, clk, clock_2_out, clock_3_out, LED_reader_1_led1, LED_reader_1_led2,
       LED_switch_1_output_1, LED_switch_1_output_2, LED_switch_1_output_3, LED_switch_1_output_4,
       LED_switch_1_output_5, LED_switch_1_output_6, LED_switch_1_output_7, LED_switch_1_output_8;

  Clock clock_1 (.out(clk));
  Clock #(.lowDuration(2)) clock_2 (.out(clock_2_out));
  Clock #(.lowDuration(4)) clock_3 (.out(clock_3_out));
  and and_1 (and_1_out, input_2, clock_2_out);
  and and_2 (and_2_out, input_3, clock_3_out);
  LED_switch LED_switch_1 (
    .en(Input_1), .next_state(clk), .Output_1(LED_switch_1_output_1), .Output_2(LED_switch_1_output_2),
    .Output_3(LED_switch_1_output_3), .Output_4(LED_switch_1_output_4), .Output_5(LED_switch_1_output_5),
    .Output_6(LED_switch_1_output_6), .Output_7(LED_switch_1_output_7), .Output_8(LED_switch_1_output_8));  // open: reset
  LED_reader LED_reader_1 (
    .input1(LED_switch_1_output_1), .input2(LED_switch_1_output_2), .input3(LED_switch_1_output_3),
    .input4(LED_switch_1_output_4), .input5(LED_switch_1_output_5), .input6(LED_switch_1_output_6),
    .input7(LED_switch_1_output_7), .input8(LED_switch_1_output_8), .LED1(LED_reader_1_led1),
    .LED2(LED_reader_1_led2), .LED3(LED3));
  or or_1 (LED1, LED_reader_1_led1, and_1_out);
  or or_2 (LED2, LED_reader_1_led2, and_2_out);
endmodule

module LED_switch (
  input  en,
  input  next_state,
  output Output_1,
  output Output_2,
  output Output_3,
  output Output_4,
  output Output_5,
  output Output_6,
  output Output_7,
  output Output_8,
  output reset
);

  wire [2:0] multiplexer_1_out, register_1_q;

  Multiplexer #(.select(4), .width(3)) multiplexer_1 (
    .in0(3'b000), .in1(3'b001), .in2(3'b010), .in3(3'b011), .in4(3'b100), .in5(3'b101), .in6(3'b110),
    .in7(3'b111), .in8(3'b001), .in9(3'b010), .in10(3'b011), .in11(3'b100), .in12(3'b101), .in13(3'b110),
    .in14(3'b111), .in15(3'b000), .out(multiplexer_1_out), .sel({en, register_1_q}));
  // Probe on multiplexer_1_out
  Register #(.width(3)) register_1 (.D(multiplexer_1_out), .Q(register_1_q), .clk(next_state));  // open: en, clr
  // Probe on register_1_q
  and and_1 (Output_1, ~register_1_q[0], ~register_1_q[1], ~register_1_q[2]);  // AND_Gate
  and and_2 (Output_2, register_1_q[0], ~register_1_q[1], ~register_1_q[2]);  // AND_Gate
  and and_3 (Output_3, ~register_1_q[0], register_1_q[1], ~register_1_q[2]);  // AND_Gate
  and and_4 (Output_4, register_1_q[0], register_1_q[1], ~register_1_q[2]);  // AND_Gate
  and and_5 (Output_5, ~register_1_q[0], ~register_1_q[1], register_1_q[2]);  // AND_Gate
  and and_6 (Output_6, register_1_q[0], ~register_1_q[1], register_1_q[2]);  // AND_Gate
  and and_7 (Output_7, ~register_1_q[0], register_1_q[1], register_1_q[2]);  // AND_Gate
  and and_8 (Output_8, register_1_q[0], register_1_q[1], register_1_q[2]);

  assign reset = next_state;
endmodule

module LED_reader (
  input  input1,
  input  input2,
  input  input3,
  input  input4,
  input  input5,
  input  input6,
  input  input7,
  input  input8,
  output LED1,
  output LED2,
  output LED3
);

  or or_1 (LED1, input1, input4, input6, input7);
  or or_2 (LED2, input2, input4, input5, input7);
  or or_3 (LED3, input3, input5, input6, input7);
endmodule
